# Fritzing sketch Circuito (saved by Fritzing 0.9.8b)
breadboards: 1

parts:
  Componente1 = Arduino Mega ADK (Rev3)
  L298N1 = L298N DC motor driver
  R1 = Rotary Potentiometer (Small) [maximum_resistance=100kΩ package=THT]
  R2 = Resistor [tolerance=±5% resistance=330 package="0402 [SMD]"]
  R3 = Resistor [tolerance=±5% resistance=330 package="0402 [SMD]"]
  DC_Mot_Enc1 = DC Motor with two-phase hall-encoder [part_number=VT-E-G25A-06-177E]
  INA1 = INA219 DC Current Sensor Breakout

nets:
  N1: Componente1.A15, R1.wiper
  N2: Componente1.D13_PWM, L298N1.ENA
  N3: Componente1.5V, R1.leg2, R2.Pin_1, R3.Pin_0, DC_Mot_Enc1.pin5
  GND: Componente1.GND, L298N1.GND, R1.leg1, DC_Mot_Enc1.pin3
  N4: Componente1.D2_PWM, R3.Pin_1, DC_Mot_Enc1.pin6
  N5: Componente1.D3_PWM, R2.Pin_0, DC_Mot_Enc1.pin4
  N6: Componente1.D6_PWM, L298N1.IN1
  N7: Componente1.D7_PWM, L298N1.IN2
  N8: L298N1.OUT1, INA1.Vin+2
  N9: L298N1.OUT2, DC_Mot_Enc1.pin2
  N10: DC_Mot_Enc1.pin1, INA1.Vin-2

custom parts:
  L298N DC motor driver: 2x DC motor driver with 78M05 positive voltage regulator (7..35 V) L298N: max 46 V, 2 A Set 5 V Enable jumper to enable 5 V regultor (needed for the L298N) and +5 V output at screw terminal or supply external +5 V at screw terminal Set ENA and/or ENB to +5 V to enable motor permanently or supply ENA and/or ENB with PWM signal IN1 and IN2 set rotation directory for motor A (OUT1/OUT2) IN2 and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
  INA219 DC Current Sensor Breakout: INA DC Current Sensor Breakout
